# Fritzing sketch necklaceFritz (saved by Fritzing 0.9.3b)
breadboards: 1

parts:
  Part1 = Adafruit NeoPixel FeatherWing [part_number="Adafruit #2945"]
  Part2 = Adafruit Feather M0 Bluefruit LE [part_number="Adafruit #2995"]
  U1 = LIPO-110mAh [package=lipo-110]  # not connected
  S1 = Momentary Switch [package=ksa_sealed_tac_switch]
  S2 = Momentary Switch [package=ksa_sealed_tac_switch]
  U2 = TMP36 [package=to-92-kit]

nets:
  +3V3: Part1.3V, Part2.AREF, Part2.+3V3, U2.VCC
  GND: Part1.GND, Part2.GND, S1.3, S1.4, S2.3, S2.4, U2.GND
  N1: Part1.I, Part2.D6
  N2: Part1.VBAT, Part2.VBAT
  N3: Part2.A3, S1.1, S1.2
  N4: Part2.A2, S2.1, S2.2
  N5: Part2.A0, U2.VOUT

custom parts:
  Adafruit NeoPixel FeatherWing: Put on your sunglasses before staring into these 32 configurable eye-blistering RGB LEDs. Arranged in a 4x8 matrix, each pixel is individually addressable. Only one pin is required to control all the LEDs. On the bottom we have jumpers for the DIN line to any of the I/O pins on a Feather. You can cut the default jumper trace and use any pin you like To make it easy to start, the LEDs are by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
  Adafruit Feather M0 Bluefruit LE: This is the Adafruit Feather M0 Bluefruit LE - our take on an 'all-in-one' Arduino-compatible + Bluetooth Low Energy with built in USB and battery charging. Its an Adafruit Feather M0 with a BTLE module, ready to rock! We have other boards in the Feather family, check'em out here. Bluetooth Low Energy is the hottest new low-power, 2.4GHz spectrum wireless protocol. In particular, its the only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
